// Logisim project RV32I.circ as structural Verilog: 14 circuits, main circuit main
module main (
  input  in_1,
  output [31:0] AC,
  output [31:0] out_3
);

  wire clk, controllogic_1_regwe;
  wire [3:0] controllogic_1_alusel;
  wire [31:0] adder_1_out, aluctl_1_datab, immediategenerator_1_imm_31_0, MAR_q, outPCT, ram_1_dout,
       regs_1_rs1, regs_1_rs2;

  Clock clock_1 (.out(clk));
  Register #(.width(32)) PC (.D(adder_1_out), .clk(clk), .Q(outPCT));  // open: en, clr
  Adder #(.width(32)) adder_1 (.a(outPCT), .b(32'h1), .out(adder_1_out));  // open: cin, cout
  Register #(.width(32)) MAR (.D(outPCT), .clk(clk), .Q(MAR_q));  // open: en, clr
  RAM #(.dataWidth(32)) ram_1 (.addr(MAR_q[7:0]), .oe(in_1), .clk(clk), .dout(ram_1_dout));  // open: we, din
  immediateGenerator immediategenerator_1 (.ins(32'h41c133), .imm_31_0(immediategenerator_1_imm_31_0));  // open: sel
  regs regs_1 (
    .rsi1(5'b00011), .rsi2(5'b00100), .rdi(5'b00010), .rd(AC), .clk(clk), .we(controllogic_1_regwe),
    .rs1(regs_1_rs1), .rs2(regs_1_rs2));
  Register #(.width(32)) MDR (.D(ram_1_dout), .clk(clk), .Q(out_3));  // open: en, clr
  Register #(.width(32)) IR (.D(out_3), .clk(clk));  // open: en, Q, clr
  ALUCtl aluctl_1 (.rs2(regs_1_rs2), .imm_31_0(immediategenerator_1_imm_31_0), .dataB(aluctl_1_datab));  // open: bsel
  ControlLogic controllogic_1 (.ins(32'h41c133), .alusel(controllogic_1_alusel), .regWe(controllogic_1_regwe));
  alu alu_1 (.A(regs_1_rs1), .B(aluctl_1_datab), .sel(controllogic_1_alusel), .AC(AC));

  // Other names for the same wires on the sheet: insT[31:0] = out_3
endmodule

module regs (
  input  [4:0] rsi1,
  input  [4:0] rsi2,
  input  [4:0] rdi,
  input  [31:0] rd,
  input  clk,
  input  we,
  output [31:0] rs1,
  output [31:0] rs2
);

  wire x0weT, x1weT, x2weT, x3weT, x4weT, x5weT, x6weT, x7weT, x8weT, x9weT, x10weT, x11weT, x12weT, x13weT,
       x14weT, x15weT, x16weT, x17weT, x18weT, x19weT, x20weT, x21weT, x22weT, x23weT, x24weT, x25weT,
       x26weT, x27weT, x28weT, x29weT, x30weT, x31weT;
  wire [31:0] x1qT, x2qT, x3qT, x4qT, x5qT, x6qT, x7qT, x8qT, x9qT, x10qT, x11qT, x12qT, x13qT, x14qT, x15qT,
       x16qT, x17qT, x18qT, x19qT, x20qT, x21qT, x22qT, x23qT, x24qT, x25qT, x26qT, x27qT, x28qT, x29qT,
       x30qT, x31qT;

  Demultiplexer #(.select(5)) demultiplexer_1 (
    .out0(x0weT), .out1(x1weT), .out2(x2weT), .out3(x3weT), .out4(x4weT), .out5(x5weT), .out6(x6weT),
    .out7(x7weT), .out8(x8weT), .out9(x9weT), .out10(x10weT), .out11(x11weT), .out12(x12weT), .out13(x13weT),
    .out14(x14weT), .out15(x15weT), .out16(x16weT), .out17(x17weT), .out18(x18weT), .out19(x19weT),
    .out20(x20weT), .out21(x21weT), .out22(x22weT), .out23(x23weT), .out24(x24weT), .out25(x25weT),
    .out26(x26weT), .out27(x27weT), .out28(x28weT), .out29(x29weT), .out30(x30weT), .out31(x31weT), .in(we),
    .sel(rdi));
  Register #(.width(32)) x4 (.D(rd), .en(x4weT), .clk(clk), .Q(x4qT));  // open: clr
  Register #(.width(32)) x8 (.D(rd), .en(x8weT), .clk(clk), .Q(x8qT));  // open: clr
  Register #(.width(32)) x12 (.D(rd), .en(x12weT), .clk(clk), .Q(x12qT));  // open: clr
  Register #(.width(32)) x16 (.D(rd), .en(x16weT), .clk(clk), .Q(x16qT));  // open: clr
  Register #(.width(32)) x20 (.D(rd), .en(x20weT), .clk(clk), .Q(x20qT));  // open: clr
  Register #(.width(32)) x24 (.D(rd), .en(x24weT), .clk(clk), .Q(x24qT));  // open: clr
  Register #(.width(32)) x28 (.D(rd), .en(x28weT), .clk(clk), .Q(x28qT));  // open: clr
  Register #(.width(32)) x2 (.D(rd), .en(x2weT), .clk(clk), .Q(x2qT));  // open: clr
  Register #(.width(32)) x6 (.D(rd), .en(x6weT), .clk(clk), .Q(x6qT));  // open: clr
  Register #(.width(32)) x10 (.D(rd), .en(x10weT), .clk(clk), .Q(x10qT));  // open: clr
  Register #(.width(32)) x14 (.D(rd), .en(x14weT), .clk(clk), .Q(x14qT));  // open: clr
  Register #(.width(32)) x18 (.D(rd), .en(x18weT), .clk(clk), .Q(x18qT));  // open: clr
  Register #(.width(32)) x22 (.D(rd), .en(x22weT), .clk(clk), .Q(x22qT));  // open: clr
  Register #(.width(32)) x26 (.D(rd), .en(x26weT), .Q(x26qT));  // open: clk, clr
  Register #(.width(32)) x30 (.D(rd), .en(x30weT), .clk(clk), .Q(x30qT));  // open: clr
  Register #(.width(32)) x1 (.D(rd), .en(x1weT), .clk(clk), .Q(x1qT));  // open: clr
  Register #(.width(32)) x5 (.D(rd), .en(x5weT), .clk(clk), .Q(x5qT));  // open: clr
  Register #(.width(32)) x9 (.D(rd), .en(x9weT), .clk(clk), .Q(x9qT));  // open: clr
  Register #(.width(32)) x13 (.D(rd), .en(x13weT), .clk(clk), .Q(x13qT));  // open: clr
  Register #(.width(32)) x17 (.D(rd), .en(x17weT), .clk(clk), .Q(x17qT));  // open: clr
  Register #(.width(32)) x21 (.D(rd), .en(x21weT), .clk(clk), .Q(x21qT));  // open: clr
  Register #(.width(32)) x25 (.D(rd), .en(x25weT), .clk(clk), .Q(x25qT));  // open: clr
  Register #(.width(32)) x29 (.D(rd), .en(x29weT), .clk(clk), .Q(x29qT));  // open: clr
  Register #(.width(32)) x3 (.D(rd), .en(x3weT), .clk(clk), .Q(x3qT));  // open: clr
  Register #(.width(32)) x7 (.D(rd), .en(x7weT), .clk(clk), .Q(x7qT));  // open: clr
  Register #(.width(32)) x11 (.D(rd), .en(x11weT), .clk(clk), .Q(x11qT));  // open: clr
  Register #(.width(32)) x15 (.D(rd), .en(x15weT), .clk(clk), .Q(x15qT));  // open: clr
  Register #(.width(32)) x19 (.D(rd), .en(x19weT), .clk(clk), .Q(x19qT));  // open: clr
  Register #(.width(32)) x23 (.D(rd), .en(x23weT), .clk(clk), .Q(x23qT));  // open: clr
  Register #(.width(32)) x27 (.D(rd), .en(x27weT), .clk(clk), .Q(x27qT));  // open: clr
  Register #(.width(32)) x31 (.D(rd), .en(x31weT), .clk(clk), .Q(x31qT));  // open: clr
  Multiplexer #(.select(5), .width(32)) multiplexer_1 (
    .in0({32{1'b0}}), .in1(x1qT), .in2(x2qT), .in3(x3qT), .in4(x4qT), .in5(x5qT), .in6(x6qT), .in7(x7qT),
    .in8(x8qT), .in9(x9qT), .in10(x10qT), .in11(x11qT), .in12(x12qT), .in13(x13qT), .in14(x14qT),
    .in15(x15qT), .in16(x16qT), .in17(x17qT), .in18(x18qT), .in19(x19qT), .in20(x20qT), .in21(x21qT),
    .in22(x22qT), .in23(x23qT), .in24(x24qT), .in25(x25qT), .in26(x26qT), .in27(x27qT), .in28(x28qT),
    .in29(x29qT), .in30(x30qT), .in31(x31qT), .out(rs1), .sel(rsi1));
  Multiplexer #(.select(5), .width(32)) multiplexer_2 (
    .in0({32{1'b0}}), .in1(x1qT), .in2(x2qT), .in3(x3qT), .in4(x4qT), .in5(x5qT), .in6(x6qT), .in7(x7qT),
    .in8(x8qT), .in9(x9qT), .in10(x10qT), .in11(x11qT), .in12(x12qT), .in13(x13qT), .in14(x14qT),
    .in15(x15qT), .in16(x16qT), .in17(x17qT), .in18(x18qT), .in19(x19qT), .in20(x20qT), .in21(x21qT),
    .in22(x22qT), .in23(x23qT), .in24(x24qT), .in25(x25qT), .in26(x26qT), .in27(x27qT), .in28(x28qT),
    .in29(x29qT), .in30(x30qT), .in31(x31qT), .out(rs2), .sel(rsi2));

  // Other names for the same wires on the sheet: rdiT[4:0] = rdi; rdT[31:0] = rd; rs1T[31:0] = rs1; rs2T[31:0] = rs2;
  //   rsi1T[4:0] = rsi1; rsi2T[4:0] = rsi2; weT = we
endmodule

module alu (
  input  [31:0] A,
  input  [31:0] B,
  input  [3:0] sel,
  output [31:0] AC
);

  wire comparator_1_lt, comparator_2_lt;
  wire [31:0] addOut, andOut, orOut, sllOut, sltOut, sltuOut, sraOut, srlOut, subOut, xorOut;

  Adder #(.width(32)) adder_1 (.a(A), .b(B), .out(addOut));  // open: cin, cout
  Subtractor #(.width(32)) subtractor_1 (.a(A), .b(B), .out(subOut));  // open: bin, bout
  Shifter #(.width(32)) shifter_1 (.in(A), .\dist (B[4:0]), .out(sllOut));
  Shifter #(.shift("lr"), .width(32)) shifter_2 (.in(A), .\dist (B[4:0]), .out(srlOut));
  Comparator #(.width(32)) comparator_1 (.a(A), .b(B), .lt(comparator_1_lt));  // open: gt, eq
  Comparator #(.mode("unsigned"), .width(32)) comparator_2 (.a(A), .b(B), .lt(comparator_2_lt));  // open: gt, eq
  assign xorOut = A ^ B;  // XOR_Gate xor_1, 32 bits wide
  Shifter #(.shift("ar"), .width(32)) shifter_3 (.in(A), .\dist (B[4:0]), .out(sraOut));
  assign orOut = A | B;  // OR_Gate or_1, 32 bits wide
  assign andOut = A & B;  // AND_Gate and_1, 32 bits wide
  assign sltOut = {{31{1'b0}}, comparator_1_lt};  // Bit_Extender bit_extender_1
  assign sltuOut = {{31{1'b0}}, comparator_2_lt};  // Bit_Extender bit_extender_2
  Multiplexer #(.select(4), .width(32)) multiplexer_1 (
    .in0(addOut), .in1(sllOut), .in2(sltOut), .in3(sltuOut), .in4(xorOut), .in5(srlOut), .in6(orOut),
    .in7(andOut), .in8(subOut), .in13(sraOut), .out(AC), .sel(sel));  // open: in9, in10, in11, in12, in14, in15

  // Other names for the same wires on the sheet: ACT[31:0] = AC; AT[31:0] = A; BT[31:0] = B; selT[3:0] = sel
endmodule

module ISplitter (
  input  [31:0] ins,
  output [6:0] opcode,
  output [4:0] rd,
  output [2:0] funct3,
  output [4:0] rs1,
  output [11:0] imm_11_0
);


  assign funct3 = ins[14:12];
  assign imm_11_0 = ins[31:20];
  assign opcode = ins[6:0];
  assign rd = ins[11:7];
  assign rs1 = ins[19:15];
endmodule

module SSplitter (
  input  [31:0] ins,
  output [6:0] opcode,
  output [4:0] imm_4_0,
  output [2:0] funct3,
  output [4:0] rs1,
  output [4:0] rs2,
  output [6:0] imm_11_5
);


  assign funct3 = ins[14:12];
  assign imm_4_0 = ins[11:7];
  assign imm_11_5 = ins[31:25];
  assign opcode = ins[6:0];
  assign rs1 = ins[19:15];
  assign rs2 = ins[24:20];
endmodule

module USplitter (
  input  [31:0] ins,
  output [6:0] opcode,
  output [4:0] rd,
  output [19:0] imm_31_12
);


  assign imm_31_12 = ins[31:12];
  assign opcode = ins[6:0];
  assign rd = ins[11:7];
endmodule

module BSplitter (
  input  [31:0] ins,
  output [6:0] opcode,
  output imm_11,
  output [3:0] imm_4_1,
  output [2:0] funct3,
  output [4:0] rs1,
  output [4:0] rs2,
  output [5:0] imm_10_5,
  output imm_12
);


  assign funct3 = ins[14:12];
  assign imm_4_1 = ins[11:8];
  assign imm_10_5 = ins[30:25];
  assign imm_11 = ins[7];
  assign imm_12 = ins[31];
  assign opcode = ins[6:0];
  assign rs1 = ins[19:15];
  assign rs2 = ins[24:20];

  // Notes on the sheet:
  //   This is the same as an S Splitter
  //   But we have specific access to the last sign bit
  //   And the MSB of the imm[4:0] field
endmodule

module JSplitter (
  input  [31:0] ins,
  output [6:0] opcode,
  output [4:0] rd,
  output [7:0] imm_19_12,
  output imm_11,
  output [9:0] imm_10_1,
  output imm_20
);


  assign imm_10_1 = ins[30:21];
  assign imm_11 = ins[20];
  assign imm_19_12 = ins[19:12];
  assign imm_20 = ins[31];
  assign opcode = ins[6:0];
  assign rd = ins[11:7];
endmodule

module immediateGenerator (
  input  [31:0] ins,
  input  [2:0] sel,
  output [31:0] imm_31_0
);

  wire imm_11;
  wire [3:0] bsplitter_1_imm_4_1;
  wire [4:0] ssplitter_1_imm_4_0;
  wire [5:0] bsplitter_1_imm_10_5;
  wire [6:0] ssplitter_1_imm_11_5;
  wire [7:0] imm_19_12;
  wire [9:0] imm_10_1;
  wire [11:0] isplitter_1_imm_11_0;
  wire [12:1] bsplitter_1_imm_11;
  wire [20:20] jsplitter_1_imm_20;
  wire [31:0] BOutT, IOutT, JOutT, SOutT;
  wire [31:12] UOutT;

  ISplitter isplitter_1 (.ins(ins), .imm_11_0(isplitter_1_imm_11_0));  // open: opcode, rd, funct3, rs1
  SSplitter ssplitter_1 (
    .ins(ins), .imm_4_0(ssplitter_1_imm_4_0), .imm_11_5(ssplitter_1_imm_11_5));  // open: opcode, funct3, rs1, rs2
  USplitter usplitter_1 (.ins(ins), .imm_31_12(UOutT));  // open: opcode, rd
  BSplitter bsplitter_1 (
    .ins(ins), .imm_11(bsplitter_1_imm_11[1]), .imm_4_1(bsplitter_1_imm_4_1),
    .imm_10_5(bsplitter_1_imm_10_5), .imm_12(bsplitter_1_imm_11[12]));  // open: opcode, funct3, rs1, rs2
  JSplitter jsplitter_1 (
    .ins(ins), .imm_19_12(imm_19_12), .imm_11(imm_11), .imm_10_1(imm_10_1), .imm_20(jsplitter_1_imm_20[20]));  // open: opcode, rd
  assign IOutT = {{20{isplitter_1_imm_11_0[11]}}, isplitter_1_imm_11_0};  // Bit_Extender bit_extender_1
  assign SOutT = {{20{ssplitter_1_imm_11_5[6]}}, {ssplitter_1_imm_11_5, ssplitter_1_imm_4_0}};  // Bit_Extender bit_extender_2
  assign BOutT = {{19{bsplitter_1_imm_11[12]}}, {bsplitter_1_imm_11[12], bsplitter_1_imm_10_5, bsplitter_1_imm_4_1, bsplitter_1_imm_11[1], 1'b0}};  // Bit_Extender bit_extender_3
  assign JOutT = {{11{jsplitter_1_imm_20[20]}}, {jsplitter_1_imm_20[20], imm_19_12, imm_11, imm_10_1, 1'b0}};  // Bit_Extender bit_extender_4
  Multiplexer #(.select(3), .width(32)) multiplexer_1 (
    .in0(IOutT), .in1(SOutT), .in2(BOutT), .in3(JOutT), .in4({UOutT, {12{1'b0}}}), .out(imm_31_0), .sel(sel));  // open: in5, in6, in7

  // Other names for the same wires on the sheet: insT[31:0] = ins; selT[2:0] = sel
endmodule

module brancher (
  input  [31:0] A,
  input  [31:0] B,
  input  brUn,
  output brEq,
  output brLT
);

  wire comparator_1_lt, comparator_2_lt;

  Comparator #(.width(32)) comparator_1 (.a(A), .b(B), .eq(brEq), .lt(comparator_1_lt));  // open: gt
  Comparator #(.mode("unsigned"), .width(32)) comparator_2 (.a(A), .b(B), .lt(comparator_2_lt));  // open: gt, eq
  Multiplexer multiplexer_1 (.in0(comparator_1_lt), .in1(comparator_2_lt), .out(brLT), .sel(brUn));

  // Other names for the same wires on the sheet: AT[31:0] = A; brEqT = brEq; brLTT = brLT; brUnT = brUn; BT[31:0] = B

  // Notes on the sheet:
  //   Use unsigned branching flag
endmodule

module pc (
  input  in_1,
  input  [31:0] inPC,
  output [31:0] outPCPlus4,
  output [31:0] outPC
);

  Register #(.width(32)) register_1 (.D(inPC), .clk(in_1), .Q(outPC));  // open: en, clr
  Adder #(.width(32)) adder_1 (.a(outPC), .b(32'h4), .out(outPCPlus4));  // open: cin, cout

  // Other names for the same wires on the sheet: clk = in_1; inPCT[31:0] = inPC; outPCPlus4T[31:0] = outPCPlus4;
  //   outPCT[31:0] = outPC
endmodule

module RSplitter (
  input  [31:0] ins,
  output [6:0] opcode,
  output [4:0] rd,
  output [2:0] funct3,
  output [4:0] rs1,
  output [4:0] rs2,
  output [6:0] funct7
);


  assign funct3 = ins[14:12];
  assign funct7 = ins[31:25];
  assign opcode = ins[6:0];
  assign rd = ins[11:7];
  assign rs1 = ins[19:15];
  assign rs2 = ins[24:20];
endmodule

module ControlLogic (
  input  [31:0] ins,
  output [3:0] alusel,
  output regWe
);

  ROM #(.addrWidth(9), .dataWidth(9)) rom_1 (.addr({ins[30], ins[14:12], ins[6:2]}));  // open: data

  // Other names for the same wires on the sheet: b2T = ins[2]; b3T = ins[3]; b4T = ins[4]; b5T = ins[5]; b6T = ins[6];
  //   b12T = ins[12]; b13T = ins[13]; b14T = ins[14]; b30T = ins[30]; regWeT = regWe

  // Notes on the sheet:
  //   contents of rom_1 (hex, n*v repeats v):
  //   12*0 1 31*0 3 31*0 5 31*0 7 31*0 9 31*0 b 31*0 d 31*0 f 31*0 11 159*0 1b
endmodule

module ALUCtl (
  input  [31:0] rs2,
  input  [31:0] imm_31_0,
  input  bsel,
  output [31:0] dataB
);

  Multiplexer #(.width(32)) multiplexer_1 (.in0(rs2), .in1(imm_31_0), .out(dataB), .sel(bsel));
endmodule
